# Fritzing sketch sweepgen (saved by Fritzing 0.9.3b)
breadboards: 2

parts:
  元件1 = Arduino Nano (Rev3.0)
  S1 = Pushbutton [package="[THT]"]
  ENCODER1 = Rotary Encoder with Knob
  OLED_I2C1 = OLED 128x64 I2C Monochrome Display
  元件2 = Adafruit Si5351A Clock Generator [part_number="Adafruit #2045"]  # not connected

nets:
  GND: 元件1.GND, S1.Pin_3, S1.Pin_4, ENCODER1.GND, OLED_I2C1.GND
  N1: 元件1.D2, ENCODER1.CLK
  N2: 元件1.D3, ENCODER1.DT
  N3: 元件1.D4, ENCODER1.SW
  N4: 元件1.D5, S1.Pin_1, S1.Pin_2
  5V: 元件1.5V, ENCODER1.+, OLED_I2C1.VDD
  N5: 元件1.A5, OLED_I2C1.SCK
  N6: 元件1.A4, OLED_I2C1.SDA

custom parts:
  Rotary Encoder with Knob: Rotary Encoder with 1/4" Shaft and Knob
  Adafruit Si5351A Clock Generator: Never hunt around for another crystal again, with the Si5351A clock generator breakout from Adafruit! This chip has a precision 25MHz crystal reference and internal PLL and dividers so it can generate just about any frequency, from <8KHz up to 150+ MHz. The Si5351A clock generator is an I2C controller clock generator. It uses the onboard precision clock to drive multiple PLL's and clock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
